# Fritzing sketch thereminIR (saved by Fritzing 0.9.2b)

parts:
  J1 = Infrared Proximity Sensor
  J2 = Infrared Proximity Sensor
  J3 = Infrared Proximity Sensor
  Composant1 = Arduino Leonardo (Rev3b)

nets:
  N1: J1.Vout, Composant1.A0
  GND: J1.GND, J2.GND, J3.GND, Composant1.GND
  VCC: J1.Vcc, J2.Vcc, J3.Vcc, Composant1.5V
  N2: J2.Vout, Composant1.A1
  N3: J3.Vout, Composant1.A2
